# Fritzing sketch insteg (saved by Fritzing 0.8.7b)
breadboards: 1

parts:
  Due = mystery part, 2 pins [chip_label=?]
  Tank1 = mystery part, 1 pin [chip_label=?]
  TS922 = LM 358 Dual Op-Amp [package="DIP8 [THT]"]
  Tank2 = mystery part, 1 pin [chip_label=?]
  R5 = Rotary Potentiometer (Small) [maximum_resistance=100kΩ package=THT]
  R6 = Rotary Potentiometer (Small) [maximum_resistance=100kΩ package=THT]
  TS9220 = LM 358 Dual Op-Amp [package="DIP8 [THT]"]
  R7 = Rotary Potentiometer (Small) [package=THT]
  part = mystery part, 1 pin
  Tank = mystery part, 1 pin
  PWM = mystery part, 1 pin

nets:
  N1: Due.pin1, TS922.connector0, TS922.connector1
  N2: Due.pin2, TS922.connector6
  N3: Tank1.pin1, R5.leg2
  N4: TS922.connector2, R5.wiper
  N5: TS922.connector4, R6.wiper
  N6: Tank2.pin1, R6.leg2
  GND: R5.leg1, R6.leg1, R7.leg1
  N7: TS9220.connector4, PWM.pin1
  N8: TS9220.connector5, R7.wiper
  N9: TS9220.connector6, Tank.pin1
  N10: R7.leg2, part.pin1

notes:
  Analog in A8 och A9. Ung. 0-2.7V
  0-10V
  ~4.9V från Due
  12V
  3.3V från Due
  Due
